// Logisim project pipelineRegisters-start.circ as structural Verilog: 5 circuits, main circuit PipeReg1
module PipeReg1 (
  input  [31:0] PC_4,
  input  [31:0] Instruction,
  input  Clock,
  input  Reset,
  output [31:0] PC_4_out,
  output [31:0] IR_out
);

  Register #(.width(32)) PC_4_Reg (.D(PC_4), .Q(PC_4_out), .clk(Clock), .clr(Reset));  // open: en
  Register #(.width(32)) IR (.D(Instruction), .Q(IR_out), .clk(Clock), .clr(Reset));  // open: en
endmodule

module PipeReg2PC (
  input  [31:0] PC_4_in,
  input  Clock,
  input  Reset,
  output [31:0] PC_4_out
);

  Register #(.width(32)) register_1 (.D(PC_4_in), .Q(PC_4_out), .clk(Clock), .clr(Reset));  // open: en
endmodule

module PipeReg2DP (
  input  [31:0] A_Register,
  input  [31:0] B_Register,
  input  [31:0] Sign_Ext,
  input  Clock,
  input  Reset,
  output [31:0] A_Reg,
  output [31:0] B_Reg,
  output [31:0] Sign_Ext_2
);

  Register #(.width(32)) u_A_reg (.D(A_Register), .Q(A_Reg), .clk(Clock), .clr(Reset));  // open: en
  Register #(.width(32)) u_B_Reg (.D(B_Register), .Q(B_Reg), .clk(Clock), .clr(Reset));  // open: en
  Register #(.width(32)) Immediate_sign_extended (.D(Sign_Ext), .Q(Sign_Ext_2), .clk(Clock), .clr(Reset));  // open: en
endmodule

module PipeReg2ALUCtrRt (
  input  [10:0] OpCode,
  input  [4:0] Rt,
  input  Clock,
  input  Reset,
  output [10:0] OpCode_out,
  output [4:0] Rt_out
);

  Register #(.width(11)) ALU_Control (.D(OpCode), .Q(OpCode_out), .clk(Clock), .clr(Reset));  // open: en
  Register #(.width(5)) u_Rt (.D(Rt), .Q(Rt_out), .clk(Clock), .clr(Reset));  // open: en
endmodule

module PipeReg2Ctrl (
  input  Unconditional_Branch,
  input  Conditional_Branch,
  input  MemToReg,
  input  MemRead,
  input  MemWrite,
  input  ALUsrc,
  input  [1:0] ALUOp,
  input  RegWrite,
  input  Clock,
  input  Reset,
  output Uncond_Branch_out,
  output Cond_Branch_out,
  output MemToReg_out,
  output MemRead_out,
  output MemWrite_2,
  output ALUsrc_out,
  output [1:0] ALUOp_out,
  output RegWrite_out
);

  Register #(.width(9)) PipelineReg2c (
    .D({RegWrite, ALUOp, ALUsrc, MemWrite, MemRead, MemToReg, Conditional_Branch, Unconditional_Branch}),
    .Q({RegWrite_out, ALUOp_out, ALUsrc_out, MemWrite_2, MemRead_out, MemToReg_out, Cond_Branch_out, Uncond_Branch_out}),
    .clk(Clock), .clr(Reset));  // open: en
endmodule
